# Fritzing sketch EPS32Car (saved by Fritzing 1.0.3b)
breadboards: 3

parts:
  M1 = ESP32-S2-DevKitC-1 [part_number=ESP32-S2-DevKitC-1]
  R1 = Photocell (LDR) [power=0.25W dark_resistance_@0.01lx=300kΩ light_resistance_@100lx=400Ω luminance=10lx package=THT]
  R2 = Resistor [tolerance=±5% resistance=220 package="0805 [SMD]"]
  SW2 = DIP Switch 8 Position [package=dipswitch-08]
  R3 = Resistor [tolerance=±5% resistance=220 package="0805 [SMD]"]
  R4 = Resistor [tolerance=±5% resistance=220 package="0805 [SMD]"]
  R5 = Resistor [tolerance=±5% resistance=220 package="0805 [SMD]"]
  R6 = Resistor [tolerance=±5% resistance=220 package="0805 [SMD]"]
  R7 = Resistor [tolerance=±5% resistance=220 package="0805 [SMD]"]
  LED1 = smd LED [color="Red (633nm)" package="0603 [SMD]"]
  LED2 = smd LED [color="Orange (620nm)" package="0603 [SMD]"]

nets:
  N1: M1.pin_1, M1.pin_2, R1.pin_1
  N2: M1.pin_22, M1.pin_23, M1.pin_24, M1.pin_44, R2.Pin_0
  N3: M1.pin_25, LED1.anode
  N4: M1.pin_27, LED2.anode
  N5: M1.pin_36, M1.pin_37, SW2.4
  N6: M1.pin_38, SW2.3
  N7: M1.pin_40, R1.pin_0, R2.Pin_1
  N8: SW2.14, R5.Pin_1
  N9: SW2.15, R4.Pin_1
  N10: SW2.16, R3.Pin_1
  N11: R3.Pin_0, R4.Pin_0, R5.Pin_0, R6.Pin_1, R7.Pin_1
  N12: R6.Pin_0, LED1.cathode
  N13: R7.Pin_0, LED2.cathode

custom parts:
  ESP32-S2-DevKitC-1: ESP32-S2-DevKitC-1 is an entry-level development board based on ESP32-S2-SOLO (on-board PCB antenna). It is based on the ESP32 microcontroller that boasts Wifi, Bluetooth, Ethernet and Low Power support all in a single chip. (vanepp) Feb 2022: converted to ESP32-S2-DevKitC-1. This module is 44pins long (2x22) and 11 pins width.
